// Logisim project CPU.circ as structural Verilog: 8 circuits, main circuit main
module main (
);

  wire clock_1_out, control_unit_1_aa, control_unit_1_bb, control_unit_1_cc, control_unit_1_j,
       control_unit_1_ramm, r_out;
  wire [3:0] rom_1_data_2;
  wire [15:0] A_q, B_q, C_q, control_unit_1_r, counter_1_q, ram_1_dout, rom_1_data;

  control_unit control_unit_1 (
    .I({rom_1_data[15], rom_1_data_2, rom_1_data[10:0]}), .A(A_q), .B(B_q), .C(C_q), .Ram(ram_1_dout),
    .R(control_unit_1_r), .aa(control_unit_1_aa), .bb(control_unit_1_bb), .cc(control_unit_1_cc),
    .ramm(control_unit_1_ramm), .j(control_unit_1_j));
  Register #(.trigger("falling"), .width(16)) A (
    .D(control_unit_1_r), .en(control_unit_1_aa), .clk(clock_1_out), .Q(A_q));  // open: clr
  RAM #(.addrWidth(4), .asyncread("true"), .dataWidth(16), .trigger("falling")) ram_1 (
    .addr(rom_1_data_2), .we(control_unit_1_ramm), .oe(1'b1), .clk(clock_1_out), .din(control_unit_1_r),
    .dout(ram_1_dout));
  // Probe on rom_1_data_2
  Register #(.trigger("falling"), .width(16)) B (
    .D(control_unit_1_r), .en(control_unit_1_bb), .clk(clock_1_out), .Q(B_q));  // open: clr
  Register #(.trigger("falling"), .width(16)) C (
    .D(control_unit_1_r), .en(control_unit_1_cc), .clk(clock_1_out), .Q(C_q));  // open: clr
  // Probe on ram_1_dout
  Counter #(.max('hffff), .width(16)) counter_1 (
    .clr(r_out), .load(control_unit_1_j), .clk(clock_1_out), .D(ram_1_dout), .Q(counter_1_q));  // open: up, count, carry
  Button r (.out(r_out));
  Clock clock_1 (.out(clock_1_out));
  ROM #(.addrWidth(16), .dataWidth(16)) rom_1 (
    .addr(counter_1_q), .data({rom_1_data[15], rom_1_data_2, rom_1_data[10:0]}));

  // Notes on the sheet:
  //   contents of rom_1 (hex, n*v repeats v):
  //   8 8710 84e0 84b0 7 fcf0 0 8404 8750 fc92 8cf0 848c 8710 2 fcf0 8c8c fc92 8c8c
endmodule

module control_unit (
  input  [15:0] I,
  input  [15:0] A,
  input  [15:0] B,
  input  [15:0] C,
  input  [15:0] Ram,
  output [15:0] R,
  output aa,
  output bb,
  output cc,
  output ramm,
  output j
);

  wire alu_instruction_1_aa, alu_instruction_1_bb, alu_instruction_1_cc, alu_instruction_1_j,
       alu_instruction_1_ramm;
  wire [15:0] alu_instruction_1_r;

  ALU_Instruction alu_instruction_1 (
    .i(I[14:0]), .A(A), .B(B), .C(C), .Ram(Ram), .R(alu_instruction_1_r), .aa(alu_instruction_1_aa),
    .bb(alu_instruction_1_bb), .cc(alu_instruction_1_cc), .Ramm(alu_instruction_1_ramm),
    .j(alu_instruction_1_j));
  control_selector control_selector_1 (
    .s(I[15]), .R0({1'b0, I[14:0]}), .A0(1'b1), .B0(1'b0), .C0(1'b0), .Ram0(1'b0), .j0(1'b0),
    .R1(alu_instruction_1_r), .A1(alu_instruction_1_aa), .B1(alu_instruction_1_bb),
    .C1(alu_instruction_1_cc), .Ram1(alu_instruction_1_ramm), .j1(alu_instruction_1_j), .R(R), .A(aa),
    .B(bb), .C(cc), .Ram(ramm), .j(j));
endmodule

module control_selector (
  input  s,
  input  [15:0] R0,
  input  A0,
  input  B0,
  input  C0,
  input  Ram0,
  input  j0,
  input  [15:0] R1,
  input  A1,
  input  B1,
  input  C1,
  input  Ram1,
  input  j1,
  output [15:0] R,
  output A,
  output B,
  output C,
  output Ram,
  output j
);

  Multiplexer #(.width(16)) multiplexer_1 (.in0(R0), .in1(R1), .out(R), .sel(s));
  Multiplexer multiplexer_2 (.in0(A0), .in1(A1), .out(A), .sel(s));
  Multiplexer multiplexer_3 (.in0(B0), .in1(B1), .out(B), .sel(s));
  Multiplexer multiplexer_4 (.in0(C0), .in1(C1), .out(C), .sel(s));
  Multiplexer multiplexer_5 (.in0(Ram0), .in1(Ram1), .out(Ram), .sel(s));
  Multiplexer multiplexer_6 (.in0(j0), .in1(j1), .out(j), .sel(s));
endmodule

module ALU_Instruction (
  input  [14:0] i,
  input  [15:0] A,
  input  [15:0] B,
  input  [15:0] C,
  input  [15:0] Ram,
  output [15:0] R,
  output aa,
  output bb,
  output cc,
  output Ramm,
  output j
);

  wire and_1_out, iszero_1_out_2, not_1_out;
  wire [15:0] multiplexer_1_out, multiplexer_1_out_2;

  Demultiplexer #(.select(2)) demultiplexer_1 (.out0(aa), .out1(bb), .out2(cc), .out3(Ramm), .in(1'b1), .sel(i[5:4]));
  Multiplexer #(.select(2), .width(32)) multiplexer_1 (
    .in0({B, A}), .in1({C, A}), .in2({C, B}), .in3({Ram, A}), .out({multiplexer_1_out_2, multiplexer_1_out}),
    .sel(i[3:2]));
  ALU alu_1 (
    .u(i[10]), .op1(i[9]), .op0(i[8]), .zw(i[7]), .sw(i[6]), .X(multiplexer_1_out), .Y(multiplexer_1_out_2),
    .out_8(R));
  not not_1 (not_1_out, iszero_1_out_2);
  iszero iszero_1 (.in_1(R), .out_2(iszero_1_out_2));
  and and_1 (and_1_out, not_1_out, i[1]);
  or or_1 (j, and_1_out, i[0]);

  // Notes on the sheet:
  //   00 AB
  //   01 AC
  //   10 BC
  //   11 A Ram
endmodule

module ALU (
  input  u,
  input  op1,
  input  op0,
  input  zw,
  input  sw,
  input  [15:0] X,
  input  [15:0] Y,
  output [15:0] out_8
);

  wire [15:0] arithmetic_unit_1_out_5, arithmetic_unit_2_out_5, logic_unit_1_out_5, logic_unit_2_out_5,
       multiplexer_1_out, multiplexer_2_out, multiplexer_3_out, multiplexer_4_out;

  Multiplexer #(.width(16)) multiplexer_1 (.in0(X), .in1({16{1'b0}}), .out(multiplexer_1_out), .sel(zw));
  Multiplexer #(.width(16)) multiplexer_2 (.in0(Y), .in1({16{1'b0}}), .out(multiplexer_2_out), .sel(zw));
  Logic_Unit logic_unit_1 (.op1(op0), .op0(op1), .X(multiplexer_1_out), .Y(Y), .out_5(logic_unit_1_out_5));
  Arithmetic_Unit arithmetic_unit_1 (
    .op1(op0), .op0(op1), .X(multiplexer_1_out), .Y(Y), .out_5(arithmetic_unit_1_out_5));
  Logic_Unit logic_unit_2 (.op1(op0), .op0(op1), .X(multiplexer_2_out), .Y(X), .out_5(logic_unit_2_out_5));
  Arithmetic_Unit arithmetic_unit_2 (
    .op1(op0), .op0(op1), .X(multiplexer_2_out), .Y(X), .out_5(arithmetic_unit_2_out_5));
  Multiplexer #(.width(16)) multiplexer_3 (
    .in0(logic_unit_1_out_5), .in1(arithmetic_unit_1_out_5), .out(multiplexer_3_out), .sel(u));
  Multiplexer #(.width(16)) multiplexer_4 (
    .in0(logic_unit_2_out_5), .in1(arithmetic_unit_2_out_5), .out(multiplexer_4_out), .sel(u));
  Multiplexer #(.width(16)) multiplexer_5 (.in0(multiplexer_3_out), .in1(multiplexer_4_out), .out(out_8), .sel(sw));
endmodule

module Arithmetic_Unit (
  input  op1,
  input  op0,
  input  [15:0] X,
  input  [15:0] Y,
  output [15:0] out_5
);

  wire [15:0] adder_1_out, adder_2_out, multiplexer_1_out, multiplexer_3_out, subtractor_1_out,
       subtractor_2_out;

  Adder #(.width(16)) adder_1 (.a(X), .b(Y), .out(adder_1_out));  // open: cin, cout
  Subtractor #(.width(16)) subtractor_1 (.a(X), .b(Y), .out(subtractor_1_out));  // open: bin, bout
  Adder #(.width(16)) adder_2 (.a(X), .b(16'h1), .out(adder_2_out));  // open: cin, cout
  Subtractor #(.width(16)) subtractor_2 (.a(X), .b(16'h1), .out(subtractor_2_out));  // open: bin, bout
  Multiplexer #(.width(16)) multiplexer_1 (
    .in0(adder_1_out), .in1(subtractor_1_out), .out(multiplexer_1_out), .sel(op0));
  Multiplexer #(.width(16)) multiplexer_2 (.in0(multiplexer_1_out), .in1(multiplexer_3_out), .out(out_5), .sel(op1));
  Multiplexer #(.width(16)) multiplexer_3 (
    .in0(adder_2_out), .in1(subtractor_2_out), .out(multiplexer_3_out), .sel(op0));
endmodule

module Logic_Unit (
  input  op1,
  input  op0,
  input  [15:0] X,
  input  [15:0] Y,
  output [15:0] out_5
);

  wire [15:0] and_1_out, multiplexer_1_out, multiplexer_3_out, not_1_out, or_1_out, xor_1_out;

  assign and_1_out = X & Y;  // AND_Gate and_1, 16 bits wide
  assign xor_1_out = X ^ Y;  // XOR_Gate xor_1, 16 bits wide
  assign or_1_out = X | Y;  // OR_Gate or_1, 16 bits wide
  assign not_1_out = ~X;  // NOT_Gate not_1, 16 bits wide
  Multiplexer #(.width(16)) multiplexer_1 (.in0(and_1_out), .in1(xor_1_out), .out(multiplexer_1_out), .sel(op1));
  Multiplexer #(.width(16)) multiplexer_2 (.in0(multiplexer_1_out), .in1(multiplexer_3_out), .out(out_5), .sel(op0));
  Multiplexer #(.width(16)) multiplexer_3 (.in0(or_1_out), .in1(not_1_out), .out(multiplexer_3_out), .sel(op1));
endmodule

module iszero (
  input  [15:0] in_1,
  output out_2
);

  wire and_1_out, and_2_out, and_3_out, and_4_out, and_5_out, and_6_out, and_7_out, and_8_out, and_9_out,
       and_10_out, and_11_out, and_12_out, and_13_out, and_14_out, not_1_out, not_2_out, not_3_out,
       not_4_out, not_5_out, not_6_out, not_7_out, not_8_out, not_9_out, not_10_out, not_11_out, not_12_out,
       not_13_out, not_14_out, not_15_out, not_16_out;

  not not_1 (not_1_out, in_1[0]);
  and and_1 (and_1_out, not_1_out, not_2_out);
  not not_2 (not_2_out, in_1[1]);
  not not_3 (not_3_out, in_1[2]);
  and and_2 (and_2_out, not_3_out, not_4_out);
  not not_4 (not_4_out, in_1[3]);
  not not_5 (not_5_out, in_1[4]);
  and and_3 (and_3_out, not_5_out, not_6_out);
  not not_6 (not_6_out, in_1[5]);
  not not_7 (not_7_out, in_1[6]);
  and and_4 (and_4_out, not_7_out, not_8_out);
  not not_8 (not_8_out, in_1[7]);
  not not_9 (not_9_out, in_1[8]);
  and and_5 (and_5_out, not_9_out, not_10_out);
  not not_10 (not_10_out, in_1[9]);
  not not_11 (not_11_out, in_1[10]);
  and and_6 (and_6_out, not_11_out, not_12_out);
  not not_12 (not_12_out, in_1[11]);
  not not_13 (not_13_out, in_1[12]);
  and and_7 (and_7_out, not_13_out, not_14_out);
  not not_14 (not_14_out, in_1[13]);
  not not_15 (not_15_out, in_1[14]);
  and and_8 (and_8_out, not_15_out, not_16_out);
  not not_16 (not_16_out, in_1[15]);
  and and_9 (and_9_out, and_1_out, and_2_out);
  and and_10 (and_10_out, and_3_out, and_4_out);
  and and_11 (and_11_out, and_5_out, and_6_out);
  and and_12 (and_12_out, and_7_out, and_8_out);
  and and_13 (and_13_out, and_9_out, and_10_out);
  and and_14 (and_14_out, and_11_out, and_12_out);
  and and_15 (out_2, and_13_out, and_14_out);
endmodule
